# Fritzing sketch Receiver_circuit (saved by Fritzing 0.9.3b)

parts:
  Part1 = Arduino Nano (Rev3.0)
  Part2 = Bluetooth HC-05 Macho
  S1 = Toggle Switch [package=THT]
  S2 = Toggle Switch [package=THT]
  LED3 = Super Flux LED blue [color=Green]
  LED4 = Super Flux LED blue [color=Blue]
  SparkFun_Pro_Micro1 = SparkFun Pro Micro [part_number=DEV-12640]
  S3 = Pushbutton [package="[THT]"]

nets:
  GND: Part1.GND, Part2.GND, LED3.cathode, LED4.cathode, SparkFun_Pro_Micro1.GND, S3.Pin_1, S3.Pin_2
  N1: Part1.D2, Part2.TXD, SparkFun_Pro_Micro1.D8
  N2: Part1.D3, Part2.RXD, SparkFun_Pro_Micro1.D9
  N3: Part1.D5, LED3.anode
  N4: Part1.5V, S1.COM
  N5: Part2.VCC, S1.L2, S2.L2
  N6: S2.COM, SparkFun_Pro_Micro1.VCC
  N7: LED4.anode, SparkFun_Pro_Micro1.D5
  N8: SparkFun_Pro_Micro1.RESET, S3.Pin_3, S3.Pin_4

custom parts:
  SparkFun Pro Micro: This tiny little board does all of the neat-o Arduino tricks that you’re familiar with: 4 channels of 10-bit ADC, 5 PWM pins, 12 DIOs as well as hardware serial connections Rx and Tx. Running at 16MHz and 5V, this board will remind you a lot of your other favorite Arduino-compatible boards but this little guy can go just about anywhere. There is a voltage regulator on board so it can accept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
